// Logisim project 3b.circ as structural Verilog: 1 circuit, main circuit main
module main (
  input  a,
  input  b,
  input  c,
  input  d,
  output out_5
);

  wire and_1_out, and_2_out, and_3_out, not_1_out, not_2_out, not_3_out;

  not not_1 (not_1_out, b);
  not not_2 (not_2_out, c);
  not not_3 (not_3_out, d);
  and and_1 (and_1_out, a, b, not_2_out);
  buf and_2 (and_2_out, not_2_out);  // AND_Gate
  and and_3 (and_3_out, not_1_out, not_3_out);
  or or_1 (out_5, and_1_out, and_2_out, and_3_out);

  // Notes on the sheet:
  //   F=ac'b+c'+d'b'
endmodule
