// Logisim project 5a.circ as structural Verilog: 1 circuit, main circuit main
module main (
  input  x,
  input  y,
  input  w,
  input  z,
  output out_5
);

  wire and_1_out, and_2_out, and_3_out, not_1_out;

  not not_1 (not_1_out, z);
  and and_1 (and_1_out, x, z);
  and and_2 (and_2_out, y, z);
  and and_3 (and_3_out, w, not_1_out);
  or or_1 (out_5, and_1_out, and_2_out, and_3_out);

  // Notes on the sheet:
  //   F(x,y,z,w)=zx+yz+wz'
endmodule
