// Logisim project 5b.circ as structural Verilog: 1 circuit, main circuit main
module main (
  input  A,
  input  C,
  input  B,
  output out_4
);

  wire and_1_out, and_2_out, not_1_out, not_2_out;

  and and_1 (and_1_out, A, C);
  not not_1 (not_1_out, C);
  and and_2 (and_2_out, not_1_out, not_2_out);
  not not_2 (not_2_out, A);
  or or_1 (out_4, and_1_out, and_2_out, B);

  // Notes on the sheet:
  //   F=A'C'+AC+B
endmodule
