// Logisim project 5c.circ as structural Verilog: 1 circuit, main circuit main
module main (
  input  A,
  input  B,
  input  C,
  input  D,
  output out_5
);

  wire and_1_out, and_2_out, and_3_out, not_1_out;

  not not_1 (not_1_out, B);
  and and_1 (and_1_out, A, B, C);
  or or_1 (out_5, and_1_out, and_2_out, and_3_out);
  and and_2 (and_2_out, not_1_out, D);
  and and_3 (and_3_out, C, D);

  // Notes on the sheet:
  //   F=ABC+CD+B'D
endmodule
