// Logisim project 3.1a.1.circ as structural Verilog: 1 circuit, main circuit main
module main (
  input  C,
  input  D,
  output F_D_prime_C
);

  wire not_1_out;

  not not_1 (not_1_out, D);
  or or_1 (F_D_prime_C, C, not_1_out);
endmodule
