// Logisim project 3.1a.2.circ as structural Verilog: 1 circuit, main circuit main
module main (
  input  C,
  input  D,
  output out_3
);

  wire nand_1_out;

  not nand_1 (nand_1_out, C);  // NAND_Gate
  or or_1 (out_3, ~nand_1_out, ~D);  // OR_Gate
endmodule
