// Logisim project 3.2a.1.circ as structural Verilog: 1 circuit, main circuit main
module main (
  input  A,
  input  D,
  input  C,
  output out_4
);

  wire nand_1_out, nand_2_out, nand_3_out;

  not nand_1 (nand_1_out, A);  // NAND_Gate
  not nand_2 (nand_2_out, D);  // NAND_Gate
  nand nand_3 (nand_3_out, nand_1_out, nand_2_out);
  nand nand_4 (out_4, nand_3_out, C);
endmodule
