// Logisim project Assignment3-AndyLee.circ as structural Verilog: 11 circuits, main circuit q2 Carry
module q1a_1 (
  input  C,
  input  D,
  output F_D_prime_C
);

  wire not_1_out;

  not not_1 (not_1_out, D);
  or or_1 (F_D_prime_C, C, not_1_out);
endmodule

module q1a_2__final (
  input  C,
  input  D,
  output out_3
);

  wire nand_1_out;

  not nand_1 (nand_1_out, C);  // NAND_Gate
  or or_1 (out_3, ~nand_1_out, ~D);  // OR_Gate
endmodule

module q1b__final (
  input  A,
  input  D,
  input  C,
  output out_4
);

  wire nand_1_out, nand_2_out, nand_3_out;

  not nand_1 (nand_1_out, A);  // NAND_Gate
  not nand_2 (nand_2_out, D);  // NAND_Gate
  nand nand_3 (nand_3_out, nand_1_out, nand_2_out);
  nand nand_4 (out_4, nand_3_out, C);
endmodule

module q2_Carry (
  input  x,
  input  y,
  output C
);

  wire nor_1_out, nor_2_out;

  not nor_1 (nor_1_out, x);  // NOR_Gate
  not nor_2 (nor_2_out, y);  // NOR_Gate
  nor nor_3 (C, nor_1_out, nor_2_out);
endmodule

module q2_Sum (
  input  x,
  input  y,
  output S
);

  wire nor_1_out, nor_2_out, nor_3_out, nor_4_out;

  nor nor_1 (nor_1_out, x, y);
  not nor_2 (nor_2_out, x);  // NOR_Gate
  not nor_3 (nor_3_out, y);  // NOR_Gate
  nor nor_4 (nor_4_out, nor_2_out, nor_3_out);
  and and_1 (S, ~nor_1_out, ~nor_4_out);  // AND_Gate
endmodule

module q2_Half_Adder (
  input  x,
  input  y,
  output S,
  output C
);

  q2_Sum sum (.x(x), .y(y), .S(S));
  q2_Carry carry (.x(x), .y(y), .C(C));
endmodule

module q2_Full_Adder (
  input  x,
  input  y,
  input  z,
  output S,
  output C
);

  wire HA_2_c, HA_c, HA_s, nor_1_out;

  q2_Half_Adder HA (.x(x), .y(y), .S(HA_s), .C(HA_c));
  q2_Half_Adder HA_2 (.x(HA_s), .y(z), .S(S), .C(HA_2_c));
  nor nor_1 (nor_1_out, HA_2_c, HA_c);
  not nor_2 (C, nor_1_out);  // NOR_Gate
endmodule

module q2_4bit__final (
  input  x3,
  input  x2,
  input  x1,
  input  x0,
  input  y3,
  input  y2,
  input  y1,
  input  y0,
  input  in_9,
  output carry,
  output s3,
  output s2,
  output s1,
  output s0
);

  wire q2_full_adder_2_c, q2_full_adder_3_c, q2_full_adder_4_c;

  q2_Full_Adder q2_full_adder_1 (.x(x3), .y(y3), .z(q2_full_adder_2_c), .S(s3), .C(carry));
  q2_Full_Adder q2_full_adder_2 (.x(x2), .y(y2), .z(q2_full_adder_3_c), .S(s2), .C(q2_full_adder_2_c));
  q2_Full_Adder q2_full_adder_3 (.x(x1), .y(y1), .z(q2_full_adder_4_c), .S(s1), .C(q2_full_adder_3_c));
  q2_Full_Adder q2_full_adder_4 (.x(x0), .y(y0), .z(in_9), .S(s0), .C(q2_full_adder_4_c));
endmodule

module q3_i_2 (
  input  w,
  input  x,
  output O_2
);

  wire nand_1_out, nand_2_out;

  not nand_1 (nand_1_out, w);  // NAND_Gate
  not nand_2 (nand_2_out, x);  // NAND_Gate
  nand nand_3 (O_2, nand_1_out, nand_2_out);
endmodule

module q3_i_1 (
  input  x,
  input  y,
  output i_1
);

  wire nand_1_out, nand_2_out, nand_3_out, nand_4_out;

  nand nand_1 (nand_1_out, y, y);
  nand nand_2 (nand_2_out, x, x);
  nand nand_3 (nand_3_out, x, nand_1_out);
  nand nand_4 (nand_4_out, nand_2_out, y);
  nand nand_5 (i_1, nand_3_out, nand_4_out);
endmodule

module q3_converter__final (
  input  i3,
  input  i2,
  input  i1,
  input  i0,
  output O3,
  output O2,
  output O1,
  output O0
);

  q3_i_2 q3_i_2_1 (.w(i3), .x(i2), .O_2(O2));
  q3_i_1 q3_i_1_1 (.x(i2), .y(i1), .i_1(O1));
  q3_i_1 q3_i_1_2 (.x(i1), .y(i0), .i_1(O0));

  assign O3 = i3;
endmodule
