// Logisim project assignment4 - Copy.circ as structural Verilog: 2 circuits, main circuit BCD-decoder
// BCD\nconverter
module BCD_decoder (
  input  A,
  input  B,
  input  C,
  input  D,
  output H,
  output I,
  output J,
  output K,
  output L,
  output M,
  output N
);

  wire not_1_out, not_2_out, not_3_out, not_4_out, or_1_out, or_2_out, or_3_out, or_4_out, or_6_out,
       or_7_out, or_8_out, or_9_out, or_10_out, or_11_out, or_12_out, or_13_out, or_14_out;

  not not_1 (not_1_out, A);
  not not_2 (not_2_out, C);
  not not_3 (not_3_out, B);
  not not_4 (not_4_out, D);
  or or_1 (or_1_out, A, B, C, not_4_out);
  or or_2 (or_2_out, not_3_out, C, D);
  or or_3 (or_3_out, not_3_out, C, not_4_out);
  or or_4 (or_4_out, not_3_out, not_2_out, D);
  or or_5 (J, B, not_2_out, D);
  or or_6 (or_6_out, not_3_out, C, D);
  or or_7 (or_7_out, not_3_out, not_2_out, not_4_out);
  or or_8 (or_8_out, A, B, C, not_4_out);
  or or_9 (or_9_out, not_3_out, C);
  or or_10 (or_10_out, not_2_out, not_4_out);
  or or_11 (or_11_out, A, B, not_4_out);
  or or_12 (or_12_out, B, not_2_out);
  or or_13 (or_13_out, A, B, C);
  or or_14 (or_14_out, not_3_out, not_2_out, not_4_out);
  and and_1 (H, or_1_out, or_2_out);
  and and_2 (I, or_3_out, or_4_out);
  and and_3 (K, or_6_out, or_7_out, or_8_out);
  and and_4 (L, or_9_out, not_4_out);
  and and_5 (M, or_10_out, or_11_out, or_12_out);
  and and_6 (N, or_13_out, or_14_out);
  LED led_1 (.in(H));
  LED led_2 (.in(I));
  LED led_3 (.in(J));
  LED led_4 (.in(K));
  LED led_5 (.in(L));
  LED led_6 (.in(M));
  LED led_7 (.in(N));
  _7_Segment_Display u_7_segment_display_1 (.g(N), .f(M), .a(H), .b(I), .e(L), .d(K), .c(J));  // open: dp
endmodule

module adder (
  input  in_1,
  input  in_2,
  input  in_3,
  input  in_4,
  input  in_5,
  input  in_6,
  input  in_7,
  input  in_8,
  output _9_detector,
  output adder_overflow
);

  wire adding_6_s0, adding_6_s1, adding_6_s2, adding_6_s3, and_1_out, and_2_out, bcd_decoder_1_h,
       bcd_decoder_1_i, bcd_decoder_1_j, bcd_decoder_1_k, bcd_decoder_1_l, bcd_decoder_1_m, bcd_decoder_1_n,
       bcd_decoder_2_h, bcd_decoder_2_i, bcd_decoder_2_j, bcd_decoder_2_k, bcd_decoder_2_l, bcd_decoder_2_m,
       bcd_decoder_2_n, q2_4bit_final_1_s0, q2_4bit_final_1_s1, q2_4bit_final_1_s2, q2_4bit_final_1_s3;

  q2_4bit__final q2_4bit_final_1 (
    .x3(in_1), .x2(in_2), .x1(in_3), .x0(in_4), .y3(in_5), .y2(in_6), .y1(in_7), .y0(in_8), .in_9(1'b0),
    .carry(adder_overflow), .s3(q2_4bit_final_1_s3), .s2(q2_4bit_final_1_s2), .s1(q2_4bit_final_1_s1),
    .s0(q2_4bit_final_1_s0));
  and and_1 (and_1_out, q2_4bit_final_1_s3, q2_4bit_final_1_s1);
  and and_2 (and_2_out, q2_4bit_final_1_s3, q2_4bit_final_1_s2);
  or or_1 (_9_detector, and_1_out, and_2_out);
  LED _1 (.in(_9_detector));
  LED led_1 (.in(adding_6_s3));
  LED led_2 (.in(adding_6_s0));
  LED led_3 (.in(adding_6_s2));
  LED led_4 (.in(adding_6_s1));
  q2_4bit__final adding_6 (
    .x3(q2_4bit_final_1_s3), .x2(q2_4bit_final_1_s2), .x1(q2_4bit_final_1_s1), .x0(q2_4bit_final_1_s0),
    .y3(1'b0), .y2(_9_detector), .y1(_9_detector), .y0(1'b0), .in_9(1'b0), .s3(adding_6_s3),
    .s2(adding_6_s2), .s1(adding_6_s1), .s0(adding_6_s0));  // open: carry
  BCD_decoder bcd_decoder_1 (
    .H(bcd_decoder_1_h), .I(bcd_decoder_1_i), .J(bcd_decoder_1_j), .K(bcd_decoder_1_k), .L(bcd_decoder_1_l),
    .M(bcd_decoder_1_m), .N(bcd_decoder_1_n), .A(adding_6_s3), .B(adding_6_s2), .C(adding_6_s1),
    .D(adding_6_s0));
  BCD_decoder bcd_decoder_2 (
    .H(bcd_decoder_2_h), .I(bcd_decoder_2_i), .J(bcd_decoder_2_j), .K(bcd_decoder_2_k), .L(bcd_decoder_2_l),
    .M(bcd_decoder_2_m), .N(bcd_decoder_2_n), .A(1'b0), .B(1'b0), .C(1'b0), .D(_9_detector));
  _7_Segment_Display u_7_segment_display_1 (
    .g(bcd_decoder_2_n), .f(bcd_decoder_2_m), .a(bcd_decoder_2_h), .b(bcd_decoder_2_i), .e(bcd_decoder_2_l),
    .d(bcd_decoder_2_k), .c(bcd_decoder_2_j));  // open: dp
  _7_Segment_Display u_7_segment_display_2 (
    .g(bcd_decoder_1_n), .f(bcd_decoder_1_m), .a(bcd_decoder_1_h), .b(bcd_decoder_1_i), .e(bcd_decoder_1_l),
    .d(bcd_decoder_1_k), .c(bcd_decoder_1_j));  // open: dp
endmodule
