// Logisim project assignment4.circ as structural Verilog: 3 circuits, main circuit BCD-decoder
module BCD_decoder (
  input  A,
  input  B,
  input  C,
  input  D,
  output H,
  output I,
  output J,
  output K,
  output L,
  output M,
  output N
);

  wire not_1_out, not_2_out, not_3_out, not_4_out, or_1_out, or_2_out, or_3_out, or_4_out, or_6_out,
       or_7_out, or_8_out, or_9_out, or_10_out, or_11_out, or_12_out, or_13_out, or_14_out;

  not not_1 (not_1_out, A);
  not not_2 (not_2_out, B);
  not not_3 (not_3_out, C);
  not not_4 (not_4_out, D);
  or or_1 (or_1_out, A, B, C, not_4_out);
  or or_2 (or_2_out, not_2_out, C, D);
  or or_3 (or_3_out, not_2_out, C, not_4_out);
  or or_4 (or_4_out, not_2_out, not_3_out, D);
  or or_5 (J, B, not_3_out, D);
  or or_6 (or_6_out, not_2_out, C, D);
  or or_7 (or_7_out, not_2_out, not_3_out, not_4_out);
  or or_8 (or_8_out, A, B, C, not_4_out);
  or or_9 (or_9_out, not_2_out, C);
  or or_10 (or_10_out, not_3_out, not_4_out);
  or or_11 (or_11_out, A, B, not_4_out);
  or or_12 (or_12_out, B, not_3_out);
  or or_13 (or_13_out, A, B, C);
  or or_14 (or_14_out, not_2_out, not_3_out, not_4_out);
  and and_1 (H, or_1_out, or_2_out);
  and and_2 (I, or_3_out, or_4_out);
  and and_3 (K, or_6_out, or_7_out, or_8_out);
  and and_4 (L, or_9_out, not_4_out);
  and and_5 (M, or_10_out, or_11_out, or_12_out);
  and and_6 (N, or_13_out, or_14_out);
  LED led_1 (.in(H));
  LED led_2 (.in(I));
  LED led_3 (.in(J));
  LED led_4 (.in(K));
  LED led_5 (.in(L));
  LED led_6 (.in(M));
  LED led_7 (.in(N));
  _7_Segment_Display u_7_segment_display_1 (.g(N), .f(M), .a(H), .b(I), .e(L), .d(K), .c(J));  // open: dp
endmodule

// 4bit-BCD
module _4bit_to_BCD_converter (
  input  in_1,
  input  in_2,
  input  in_3,
  input  in_4,
  input  in_5,
  output out_6,
  output out_7,
  output out_8,
  output out_9,
  output out_10
);

  wire and_1_out, and_2_out, or_2_out, q2_4bit_final_1_carry;

  and and_1 (and_1_out, in_2, in_3);
  and and_2 (and_2_out, in_2, in_4);
  or or_1 (out_6, in_1, q2_4bit_final_1_carry);
  or or_2 (or_2_out, in_1, and_1_out, and_2_out);
  q2_4bit__final q2_4bit_final_1 (
    .x3(1'b0), .x2(or_2_out), .x1(or_2_out), .x0(1'b0), .y3(in_2), .y2(in_3), .y1(in_4), .y0(in_5),
    .in_9(1'b0), .carry(q2_4bit_final_1_carry), .s3(out_7), .s2(out_8), .s1(out_9), .s0(out_10));
endmodule

module Part2_final (
  input  in_1,
  input  in_2,
  input  in_3,
  input  in_4,
  input  in_5,
  input  in_6,
  input  in_7,
  input  in_8
);

  wire bcd_decoder_1_h, bcd_decoder_1_i, bcd_decoder_1_j, bcd_decoder_1_k, bcd_decoder_1_l, bcd_decoder_1_m,
       bcd_decoder_1_n, bcd_decoder_2_h, bcd_decoder_2_i, bcd_decoder_2_j, bcd_decoder_2_k, bcd_decoder_2_l,
       bcd_decoder_2_m, bcd_decoder_2_n, n4bit_to_bcd_converter_1_out_6, n4bit_to_bcd_converter_1_out_7,
       n4bit_to_bcd_converter_1_out_8, n4bit_to_bcd_converter_1_out_9, n4bit_to_bcd_converter_1_out_10,
       n4bit_to_bcd_converter_2_out_6, n4bit_to_bcd_converter_2_out_7, n4bit_to_bcd_converter_2_out_8,
       n4bit_to_bcd_converter_2_out_9, n4bit_to_bcd_converter_2_out_10, n4bit_to_bcd_converter_3_out_6,
       n4bit_to_bcd_converter_3_out_7, n4bit_to_bcd_converter_3_out_8, n4bit_to_bcd_converter_3_out_9,
       n4bit_to_bcd_converter_3_out_10, q2_4bit_final_1_s0, q2_4bit_final_1_s1, q2_4bit_final_1_s2,
       q2_4bit_final_1_s3, q2_4bit_final_2_carry, q2_4bit_final_2_s0, q2_4bit_final_2_s1, q2_4bit_final_2_s2,
       q2_4bit_final_2_s3;

  _4bit_to_BCD_converter u_4bit_to_bcd_converter_1 (
    .out_6(n4bit_to_bcd_converter_1_out_6), .out_7(n4bit_to_bcd_converter_1_out_7),
    .out_8(n4bit_to_bcd_converter_1_out_8), .out_9(n4bit_to_bcd_converter_1_out_9),
    .out_10(n4bit_to_bcd_converter_1_out_10), .in_1(1'b0), .in_2(in_1), .in_3(in_2), .in_4(in_3), .in_5(in_4));
  _4bit_to_BCD_converter u_4bit_to_bcd_converter_2 (
    .out_6(n4bit_to_bcd_converter_2_out_6), .out_7(n4bit_to_bcd_converter_2_out_7),
    .out_8(n4bit_to_bcd_converter_2_out_8), .out_9(n4bit_to_bcd_converter_2_out_9),
    .out_10(n4bit_to_bcd_converter_2_out_10), .in_1(1'b0), .in_2(in_5), .in_3(in_6), .in_4(in_7), .in_5(in_8));
  q2_4bit__final q2_4bit_final_1 (
    .x3(1'b0), .x2(1'b0), .x1(1'b0), .x0(n4bit_to_bcd_converter_1_out_6), .y3(1'b0), .y2(1'b0), .y1(1'b0),
    .y0(n4bit_to_bcd_converter_2_out_6), .in_9(n4bit_to_bcd_converter_3_out_6), .s3(q2_4bit_final_1_s3),
    .s2(q2_4bit_final_1_s2), .s1(q2_4bit_final_1_s1), .s0(q2_4bit_final_1_s0));  // open: carry
  _4bit_to_BCD_converter u_4bit_to_bcd_converter_3 (
    .out_6(n4bit_to_bcd_converter_3_out_6), .out_7(n4bit_to_bcd_converter_3_out_7),
    .out_8(n4bit_to_bcd_converter_3_out_8), .out_9(n4bit_to_bcd_converter_3_out_9),
    .out_10(n4bit_to_bcd_converter_3_out_10), .in_1(q2_4bit_final_2_carry), .in_2(q2_4bit_final_2_s3),
    .in_3(q2_4bit_final_2_s2), .in_4(q2_4bit_final_2_s1), .in_5(q2_4bit_final_2_s0));
  q2_4bit__final q2_4bit_final_2 (
    .x3(n4bit_to_bcd_converter_1_out_7), .x2(n4bit_to_bcd_converter_1_out_8),
    .x1(n4bit_to_bcd_converter_1_out_9), .x0(n4bit_to_bcd_converter_1_out_10),
    .y3(n4bit_to_bcd_converter_2_out_7), .y2(n4bit_to_bcd_converter_2_out_8),
    .y1(n4bit_to_bcd_converter_2_out_9), .y0(n4bit_to_bcd_converter_2_out_10), .in_9(1'b0),
    .carry(q2_4bit_final_2_carry), .s3(q2_4bit_final_2_s3), .s2(q2_4bit_final_2_s2), .s1(q2_4bit_final_2_s1),
    .s0(q2_4bit_final_2_s0));
  BCD_decoder bcd_decoder_1 (
    .H(bcd_decoder_1_h), .I(bcd_decoder_1_i), .J(bcd_decoder_1_j), .K(bcd_decoder_1_k), .L(bcd_decoder_1_l),
    .M(bcd_decoder_1_m), .N(bcd_decoder_1_n), .A(q2_4bit_final_1_s3), .B(q2_4bit_final_1_s2),
    .C(q2_4bit_final_1_s1), .D(q2_4bit_final_1_s0));
  BCD_decoder bcd_decoder_2 (
    .H(bcd_decoder_2_h), .I(bcd_decoder_2_i), .J(bcd_decoder_2_j), .K(bcd_decoder_2_k), .L(bcd_decoder_2_l),
    .M(bcd_decoder_2_m), .N(bcd_decoder_2_n), .A(n4bit_to_bcd_converter_3_out_7),
    .B(n4bit_to_bcd_converter_3_out_8), .C(n4bit_to_bcd_converter_3_out_9),
    .D(n4bit_to_bcd_converter_3_out_10));
  _7_Segment_Display u_7_segment_display_1 (
    .g(bcd_decoder_1_n), .f(bcd_decoder_1_m), .a(bcd_decoder_1_h), .b(bcd_decoder_1_i), .e(bcd_decoder_1_l),
    .d(bcd_decoder_1_k), .c(bcd_decoder_1_j));  // open: dp
  _7_Segment_Display u_7_segment_display_2 (
    .g(bcd_decoder_2_n), .f(bcd_decoder_2_m), .a(bcd_decoder_2_h), .b(bcd_decoder_2_i), .e(bcd_decoder_2_l),
    .d(bcd_decoder_2_k), .c(bcd_decoder_2_j));  // open: dp
endmodule
